// Logisim project e2236891.circ as structural Verilog: 1 circuit, main circuit main
module main (
  input  A1,
  input  A0,
  input  B1,
  input  B0,
  input  S0,
  input  S1,
  output Y0,
  output Y1,
  output Y2,
  output Y3,
  output Y4,
  output Y5,
  output Y6,
  output Y7,
  output X2,
  output X1,
  output X0
);

  wire and_1_out, and_2_out, and_3_out, and_4_out, and_5_out, n3_to_8_decoder_74138_1_p7,
       n3_to_8_decoder_74138_1_p8, n3_to_8_decoder_74138_1_p9, n3_to_8_decoder_74138_1_p10,
       n3_to_8_decoder_74138_1_p11, n3_to_8_decoder_74138_1_p12, n3_to_8_decoder_74138_1_p13,
       n3_to_8_decoder_74138_1_p14, not_1_out, not_2_out, not_3_out, not_4_out, not_5_out, or_1_out,
       or_2_out, or_3_out, or_4_out, xor_1_out, xor_2_out, xor_3_out;

  not not_1 (not_1_out, and_3_out);
  not not_2 (not_2_out, A0);
  and and_1 (and_1_out, A0, not_1_out);
  and and_2 (and_2_out, B0, or_1_out);
  not not_3 (not_3_out, A1);
  and and_3 (and_3_out, not_3_out, B1);
  and and_4 (and_4_out, not_2_out, B0);
  or or_1 (or_1_out, not_3_out, B1);
  or or_2 (or_2_out, and_1_out, and_2_out);
  and and_5 (and_5_out, and_4_out, or_1_out);
  xor xor_1 (xor_1_out, A1, B1);
  not not_4 (not_4_out, and_4_out);
  xor xor_2 (xor_2_out, A0, B0);
  or or_3 (or_3_out, and_3_out, and_5_out);
  xor xor_3 (xor_3_out, xor_1_out, not_4_out);
  or or_4 (or_4_out, B1, A1);
  not not_5 (not_5_out, xor_3_out);
  // _4_to_1_MUX__x2___74153 #(.Facing("east")) 4_to_1_mux_x2_74153_1: pin names not known; wires that end beside it: or_3_out, 1'b0, B1, A1, 1'b0, X2
  // _4_to_1_MUX__x2___74153 #(.Facing("east")) 4_to_1_mux_x2_74153_2: pin names not known; wires that end beside it: not_5_out, or_4_out, B0, A0, S0, 1'b0, S1, X1
  // _4_to_1_MUX__x2___74153 #(.Facing("east")) 4_to_1_mux_x2_74153_3: pin names not known; wires that end beside it: xor_2_out, or_2_out, 1'b0, 1'b1, S0, 1'b0, S0, S1, S1, X0
  // _3_to_8_decoder__74138 #(.Facing("east")) 3_to_8_decoder_74138_1: pin names not known; wires that end beside it: X0, X1, X2, 1'b1, 1'b0, 1'b0, n3_to_8_decoder_74138_1_p7, n3_to_8_decoder_74138_1_p8, n3_to_8_decoder_74138_1_p9, n3_to_8_decoder_74138_1_p10, n3_to_8_decoder_74138_1_p11, n3_to_8_decoder_74138_1_p12, n3_to_8_decoder_74138_1_p13, n3_to_8_decoder_74138_1_p14
  not not_6 (Y2, n3_to_8_decoder_74138_1_p9);
  not not_7 (Y1, n3_to_8_decoder_74138_1_p8);
  not not_8 (Y0, n3_to_8_decoder_74138_1_p7);
  not not_9 (Y3, n3_to_8_decoder_74138_1_p10);
  not not_10 (Y5, n3_to_8_decoder_74138_1_p12);
  not not_11 (Y6, n3_to_8_decoder_74138_1_p13);
  not not_12 (Y4, n3_to_8_decoder_74138_1_p11);
  not not_13 (Y7, n3_to_8_decoder_74138_1_p14);
endmodule
